# Fritzing sketch prototype_breadboard (saved by Fritzing 0.9.2b)
breadboards: 1

parts:
  J1 = Peltier Element
  Q1 = Basic FET N-Channel [package="TO220 [THT]"]
  R1 = Resistor [tolerance=±5% resistance=220 package=THT]
  LED1 = LED - 5mm [color="Red (633nm)" package="5 mm [THT]"]
  R2 = Resistor [tolerance=±5% resistance=220 package=THT]
  Part1 = Adafruit Metro Mini [part_number="Adafruit #2590"]
  Part2 = Adafruit MicroSD card breakout board [part_number="Adafruit #254"]
  Part3 = Adafruit SHT31-D Sensirion Temperature/Humidity Sensor [part_number="Adafruit #2857"]
  Part4 = Adafruit TSL2561 [part_number="Adafruit #439"]
  Part6 = LilyPad Coin Cell Battery Holder
  IC1 = DS1302 [package="SO8 [SMD]"]
  Part5 = JeePlug experimenter's board
  XTAL1 = CRYSTAL - kHz [frequency="32 kHz"]
  LED2 = LED - 3mm [color="Red (633nm)" package="3 mm [THT]"]

nets:
  GND: J1.pin1, LED1.anode, Part1.GND, Part2.GND, Part3.GND, Part4.GND, IC1.+V, Part5.B2, Part5.N$12
  N1: J1.pin2, Q1.source
  N2: Q1.gate, Part1.IO3
  N3: R1.Pin_0, Part1.IO6
  N4: R1.Pin_1, LED2.cathode
  N5: LED1.cathode, R2.Pin_1
  N6: R2.Pin_0, Part1.IO5
  N7: Part1.AD5/SCL, Part3.SCL, Part4.SCL
  N8: Part1.AD4/SDA, Part3.SDA, Part4.SDA
  N9: Part1.IO13, Part2.CLK
  N10: Part1.IO12, Part2.DO
  N11: Part1.IO11, Part2.DI
  N12: Part1.IO10, Part2.CS
  N13: Part1.IO9, IC1.CE_-_Chip_Enable, Part5.B5, Part5.N$38
  N14: Part1.IO8, IC1.I/O_-_SPI_Data_In/Out, Part5.B4, Part5.N$36
  N15: Part1.IO7, IC1.SCLK_-_SPI_Clock, Part5.B3, Part5.N$35
  VIN: Part1.+5V, Part2.VCC, Part3.VIN, Part4.VIN, Part6.+, IC1.0V, IC1.Vbat_-_Backup_Supply, Part5.B1, Part5.N$15, Part5.N$34
  N16: IC1.X1_-_Crystal, Part5.N$7, Part5.N$13, XTAL1.pin_0
  N17: IC1.X2_-_Crystal, Part5.N$14, Part5.N$16, XTAL1.pin_1

custom parts:
  Adafruit Metro Mini: We sure love the ATmega328 here at Adafruit, and we use them a lot for our own projects. The processor has plenty of GPIO, Analog inputs, hardware UART SPI and I2C, timers and PWM galore - just enough for most simple projects. When we need to go small, we use a Pro Trinket 3V or 5V, but if you want to have USB-to-Serial built in, we reach for an Adafruit METRO Mini. METRO Mini is the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
  Adafruit MicroSD card breakout board: Not just a simple breakout board, this microSD adapter goes the extra mile - designed for ease of use. Onboard 5v->3v regulator provides 150mA for power-hungry cards 3v level shifting means you can use this with ease on either 3v or 5v systems Uses a proper level shifting chip, not resistors: less problems, and faster read/write access Use 3 or 4 digital pins to read and write 2Gb+ of storage!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
  Adafruit SHT31-D Sensirion Temperature/Humidity Sensor: Sensirion Temperature/Humidity sensors are some of the finest & highest-accuracy devices you can get. And, finally we have some that have a true I2C interface for easy reading. The SHT31-D sensor has an excellent ±2% relative humidity and ±0.3°C accuracy for most uses. Unlike earlier SHT sensors, this sensor has a true I2C interface, and (bonus!) even with two address options. It also is 3V or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
  Adafruit TSL2561: The TSL2561 luminosity sensor is an advanced digital light sensor, ideal for use in a wide range of light situations. Compared to low cost CdS cells, this sensor is more precise, allowing for exact lux calculations and can be configured for different gain/timing ranges to detect light ranges from up to 0.1 - 40,000+ Lux on the fly. The best part of this sensor is that it contains both infrared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
