# Fritzing sketch prototype_breadboard (saved by Fritzing 0.9.2b)
circuit board: 4.46912cm x 2.45958cm
circuit board: 5.1061cm x 6.54499cm
circuit board: 4.97431cm x 2.02028cm
breadboards: 1

parts:
  Part1 = Adafruit Metro Mini [part_number="Adafruit #2590"]
  Part3 = Adafruit SHT31-D Sensirion Temperature/Humidity Sensor [part_number="Adafruit #2857"]
  Part4 = Adafruit TSL2561 [part_number="Adafruit #439"]
  Q1 = Basic FET N-Channel [part_number=IRLB8721PbF package="TO220 [THT]"]
  Peltier_(sandwiched_between_heat_skinks_and_fan) = Peltier Element
  4-pin_fan_(inside) = Header 4 [package=screwterminal-3.5mm-4_lock]
  4-pin_fan_(outside) = Header 4 [package=screwterminal-3.5mm-4_lock]
  internal_sensor_hub = Header 4 [package=screwterminal-3.5mm-4_lock]
  Part5 = Adafruit MicroSD card breakout board [part_number="Adafruit #254"]
  Part6 = Adafruit PCF8523 RTC [part_number="Adafruit #3295"]
  4-pin_fan_(inside)1 = Header 4 [package=screwterminal-3.5mm-4_lock]
  4-pin_fan_(outside)1 = Header 4 [package=screwterminal-3.5mm-4_lock]
  Peltier_(sandwiched_between_heat_skinks_and_fan)1 = Peltier Element
  Q2 = TIP120 Hi-Current Darlington Transistor
  12V_strip_of_white_LED_#3 = LEDs [package=led-1206]
  12V_strip_of_white_LED_#2 = LEDs [package=led-1206]
  12V_strip_of_white_LED_#3_2 = LEDs [package=led-1206]
  U2 = DC-DC Buck Converter [package=dc-dc_converter]
  Switching_12V_power_supply = Power plug

nets (from the schematic view):
  N1: Part1.AD5/SCL, Part3.SCL, Part4.SCL, internal_sensor_hub.2, Part6.SCL
  N2: Part1.AD4/SDA, Part3.SDA, Part4.SDA, internal_sensor_hub.1, Part6.SDA
  N3: Part1.IO13, Part5.CLK
  N4: Part1.IO12, Part5.DO
  N5: Part1.IO11, Part5.DI
  N6: Part1.IO10, Part5.CS
  N7: Part1.IO9, Part5.CD
  N8: Part1.IO5, Q1.gate
  N9: Part1.IO4, Q2.BASE
  N10: Part1.IO3, 4-pin_fan_(inside).4, 4-pin_fan_(outside).4, 4-pin_fan_(inside)1.4, 4-pin_fan_(outside)1.4
  3.3V: Part1.3.3V, Part5.+3V3
  VIN: Part1.+5V, Part3.VIN, Part4.VIN, internal_sensor_hub.3, Part6.VCC
  GND: Part1.GND, Part3.GND, Part4.GND, Q1.drain, Q1.source, Peltier_(sandwiched_between_heat_skinks_and_fan).pin1, 4-pin_fan_(inside).1, 4-pin_fan_(outside).1, internal_sensor_hub.4, Part5.GND, Part6.GND, 4-pin_fan_(inside)1.1, 4-pin_fan_(outside)1.1, Peltier_(sandwiched_between_heat_skinks_and_fan)1.pin1, Q2.EMITTER, U2.OUT-_2, U2.IN-_2, Switching_12V_power_supply.GND
  N11: Peltier_(sandwiched_between_heat_skinks_and_fan).pin2, 4-pin_fan_(inside).2, 4-pin_fan_(outside).2, 4-pin_fan_(inside)1.2, 4-pin_fan_(outside)1.2, Peltier_(sandwiched_between_heat_skinks_and_fan)1.pin2, 12V_strip_of_white_LED_#3.C, 12V_strip_of_white_LED_#2.A, 12V_strip_of_white_LED_#3_2.C, U2.OUT+_1, U2.OUT+_2, U2.IN+_2, U2.IN+_1, Switching_12V_power_supply.VCC
  N12: Q2.COLLECTOR, 12V_strip_of_white_LED_#3.A, 12V_strip_of_white_LED_#2.C, 12V_strip_of_white_LED_#3_2.A
  N13: U2.OUT-_1, U2.IN-_1

custom parts:
  Adafruit Metro Mini: We sure love the ATmega328 here at Adafruit, and we use them a lot for our own projects. The processor has plenty of GPIO, Analog inputs, hardware UART SPI and I2C, timers and PWM galore - just enough for most simple projects. When we need to go small, we use a Pro Trinket 3V or 5V, but if you want to have USB-to-Serial built in, we reach for an Adafruit METRO Mini. METRO Mini is the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
  Adafruit SHT31-D Sensirion Temperature/Humidity Sensor: Sensirion Temperature/Humidity sensors are some of the finest & highest-accuracy devices you can get. And, finally we have some that have a true I2C interface for easy reading. The SHT31-D sensor has an excellent ±2% relative humidity and ±0.3°C accuracy for most uses. Unlike earlier SHT sensors, this sensor has a true I2C interface, and (bonus!) even with two address options. It also is 3V or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
  Adafruit TSL2561: The TSL2561 luminosity sensor is an advanced digital light sensor, ideal for use in a wide range of light situations. Compared to low cost CdS cells, this sensor is more precise, allowing for exact lux calculations and can be configured for different gain/timing ranges to detect light ranges from up to 0.1 - 40,000+ Lux on the fly. The best part of this sensor is that it contains both infrared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
  Adafruit MicroSD card breakout board: Not just a simple breakout board, this microSD adapter goes the extra mile - designed for ease of use. Onboard 5v->3v regulator provides 150mA for power-hungry cards 3v level shifting means you can use this with ease on either 3v or 5v systems Uses a proper level shifting chip, not resistors: less problems, and faster read/write access Use 3 or 4 digital pins to read and write 2Gb+ of storage!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
  Adafruit PCF8523 RTC: This is a great battery-backed real time clock (RTC) that allows your microcontroller project to keep track of time even if it is reprogrammed, or if the power is lost. Perfect for datalogging, clock-building, time stamping, timers and alarms, etc. Equipped with PCF8523 RTC - it can run from 3.3V or 5V power & logic! Works great with an Arduino using our RTC library, with CircuitPython or with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
  DC-DC Buck Converter: eBoot Mini MP1584EN DC-DC Buck Converter Adjustable Power Step Down Module 24V to 12V 9V 5V 3V
